// Logisim project control.circ as structural Verilog: 1 circuit, main circuit main
// Control Unit
module main (
  input  CLK,
  input  [3:0] Cond,
  input  PCSrc,
  input  [1:0] Op,
  input  RegWrite,
  input  [5:0] Funct,
  input  MemWrite,
  input  [3:0] Rd,
  input  MemtoReg,
  input  [3:0] ALUFlags,
  input  ALUSrc,
  input  [1:0] ImmSrc,
  input  [3:0] ALUControl,
  input  [1:0] RegSrc
);

  wire decoder_1_out0, decoder_1_out1, decoder_1_out2, decoder_2_out0, decoder_2_out1, decoder_3_out0,
       decoder_3_out1, DP_Imm_out, DP_Reg_out, LDR_out, not_1_out, not_2_out, not_3_out, not_4_out,
       not_5_out, STR_out, undriven_2, undriven_3, undriven_4;
  wire [1:0] and_1_out, undriven, undriven_5;

  Decoder #(.select(2), .enable("false")) decoder_1 (
    .out0(decoder_1_out0), .out1(decoder_1_out1), .out2(decoder_1_out2), .sel(Op));  // open: out3
  Decoder #(.enable("false")) decoder_2 (.out0(decoder_2_out0), .out1(decoder_2_out1), .sel(Funct[0]));
  Decoder #(.enable("false")) decoder_3 (.out0(decoder_3_out0), .out1(decoder_3_out1), .sel(Funct[5]));
  not not_1 (not_1_out, DP_Reg_out);
  and DP_Reg (DP_Reg_out, decoder_1_out0, decoder_3_out0);
  not not_2 (not_2_out, DP_Imm_out);
  and DP_Imm (DP_Imm_out, decoder_1_out0, decoder_3_out1);
  not not_3 (not_3_out, STR_out);
  and STR (STR_out, decoder_1_out1, decoder_2_out0);
  not not_4 (not_4_out, LDR_out);
  and LDR (LDR_out, decoder_1_out1, decoder_2_out1);
  not not_5 (not_5_out, decoder_1_out2);
  assign and_1_out = undriven & undriven_5;  // AND_Gate and_1, 2 bits wide
  and and_2 (PCSrc, undriven_2, undriven_5[0]);
  and and_3 (RegWrite, undriven_3, undriven_5[0]);
  and and_4 (MemWrite, undriven_4, undriven_5[0]);
  // alu_control_main main_1: pin names not known

  // Notes on the sheet:
  //   Main Decoder
endmodule
