// Logisim project cpu.circ as structural Verilog: 1 circuit, main circuit main
module main (
  input  [31:0] INSTRUCTION,
  input  CLOCK,
  output [31:0] FETCH_ADDRESS,
  output [31:0] R0_Value,
  output [31:0] R1_Value,
  output [31:0] R2_Value,
  output [31:0] LR_Value,
  output [31:0] SP_Value
);

  wire ALUSrc, MemtoReg, MemWrite, PCSrc, RegWrite;
  wire [1:0] ImmSrc, RegSrc;
  wire [3:0] ALUControl, ALUFlags, RA1, RA2;
  wire [31:0] adder_1_out, Data_Memory_read_data, ExtImm8, ExtImm12, ExtImm24, main_1_read_data_1,
       main_2_result, multiplexer_3_out, multiplexer_4_out, multiplexer_6_out, R15, SrcB, WD3;

  Multiplexer #(.width(4), .enable("false")) multiplexer_1 (
    .in0(INSTRUCTION[19:16]), .in1(4'b1111), .out(RA1), .sel(RegSrc[1]));
  Multiplexer #(.width(4), .enable("false")) multiplexer_2 (
    .in0(INSTRUCTION[3:0]), .in1(INSTRUCTION[15:12]), .out(RA2), .sel(RegSrc[0]));
  assign ExtImm8 = {{24{1'b0}}, INSTRUCTION[7:0]};  // Bit_Extender bit_extender_1
  assign ExtImm12 = {{20{1'b0}}, INSTRUCTION[11:0]};  // Bit_Extender bit_extender_2
  assign ExtImm24 = {{8{INSTRUCTION[23]}}, INSTRUCTION[23:0]};  // Bit_Extender bit_extender_3
  regfile_main main_1 (
    .Read_Register_1(RA1), .Read_Register_2(RA2), .Write_Register(INSTRUCTION[15:12]), .Write_Data(WD3),
    .Write_Enable(RegWrite), .Clock(CLOCK), .Read_Data_1(main_1_read_data_1), .Read_Data_2(SrcB),
    .R0_Value(R0_Value), .R1_Value(R1_Value), .R3_Value(R2_Value), .LR__R14__Value(LR_Value),
    .SP__R13__Value(SP_Value), .R15(R15));
  Multiplexer #(.select(2), .width(32), .enable("false")) multiplexer_3 (
    .in0(ExtImm8), .in1(ExtImm12), .in2(ExtImm24), .out(multiplexer_3_out), .sel(ImmSrc));  // open: in3
  Multiplexer #(.width(32), .enable("false")) multiplexer_4 (
    .in0(SrcB), .in1(multiplexer_3_out), .out(multiplexer_4_out), .sel(ALUSrc));
  alu_main main_2 (
    .ALUControl(ALUControl), .A(main_1_read_data_1), .ALUFlags(ALUFlags), .Result(main_2_result),
    .B(multiplexer_4_out));
  Multiplexer #(.width(32), .enable("false")) multiplexer_5 (
    .in0(main_2_result), .in1(Data_Memory_read_data), .out(WD3), .sel(MemtoReg));
  mem_main Data_Memory (
    .Address(main_2_result), .Write_Data(SrcB), .Write_En(MemWrite), .Clock(CLOCK),
    .Read_Data(Data_Memory_read_data));
  Register #(.width(32)) PC (.D(multiplexer_6_out), .Q(FETCH_ADDRESS), .clk(CLOCK));  // open: en, clr
  Multiplexer #(.width(32), .enable("false")) multiplexer_6 (
    .in0(adder_1_out), .in1(WD3), .out(multiplexer_6_out), .sel(PCSrc));
  Adder #(.width(32)) adder_1 (.a(FETCH_ADDRESS), .b(32'h4), .out(adder_1_out));  // open: cin, cout
  control_main main_3 (
    .Cond(INSTRUCTION[31:28]), .Op(INSTRUCTION[27:26]), .Funct(INSTRUCTION[25:20]), .Rd(INSTRUCTION[15:12]),
    .ALUFlags(ALUFlags), .PCSrc(PCSrc), .MemtoReg(MemtoReg), .MemWrite(MemWrite), .ALUControl(ALUControl),
    .ALUSrc(ALUSrc), .ImmSrc(ImmSrc), .RegWrite(RegWrite), .RegSrc(RegSrc));  // open: CLK
  Adder #(.width(32)) adder_2 (.a(adder_1_out), .b(32'h4), .out(R15));  // open: cin, cout

  // Other names for the same wires on the sheet: clk = CLOCK; fetch_addr[31:0] = FETCH_ADDRESS;
  //   RA3[3:0] = INSTRUCTION[15:12]; Rd[3:0] = INSTRUCTION[15:12]; Funct[5:0] = INSTRUCTION[25:20];
  //   Op[1:0] = INSTRUCTION[27:26]; Cond[3:0] = INSTRUCTION[31:28]; R0[31:0] = R0_Value; R1[31:0] = R1_Value;
  //   R2[31:0] = R2_Value; R13[31:0] = SP_Value; R14[31:0] = LR_Value

  // Notes on the sheet:
  //   Branch
  //   Instruction Memory
  //   Output
  //   Hongwei Cai
  //   ARM Processor
  //   Computer Organization
  //   Spring 2022
  //   Inputs
  //   These are DEBUG/TEST outputs from your circuit.
  //   PC+4
  //   PC+8
endmodule
